# Fritzing sketch IOT_ESP32 (saved by Fritzing 0.9.3b)
breadboards: 1

parts:
  DOIT_ESP32 = Adafruit HUZZAH32 ESP32 Feather [part_number="Adafruit #3405"]
  DHT1 = DHT11 Humitidy and Temperature Sensor
  photoresistor = PHOTOCELL [package=photocell-kit]
  BUZZ = Piezo Speaker
  R2 = Rotary Potentiometer (Small) [maximum_resistance=10kΩ package=THT]
  LED1 = LED - 5mm [color="Green (555nm)" package="5 mm [THT]"]
  LED2 = LED - 5mm [color="Red (635nm)" package="5 mm [THT]"]
  R3 = Resistor [tolerance=±5% resistance=220 package=THT]
  R4 = Resistor [tolerance=±5% resistance=220 package=THT]  # not connected
  R5 = Resistor [tolerance=±5% resistance=10k package=THT]

nets:
  N1: DOIT_ESP32.MOSI, BUZZ.pin2
  N2: DOIT_ESP32.A4_IO36, DHT1.DATA
  N3: DOIT_ESP32.A3_I39, LED1.anode
  N4: DOIT_ESP32.A2_I34, LED2.anode
  N5: DOIT_ESP32.VBAT, DHT1.VDD, photoresistor.P$2, R2.leg2
  N6: DOIT_ESP32.EN, DHT1.GND, BUZZ.pin1, R2.leg1, R5.Pin_1
  N7: DOIT_ESP32.IO14_A6, R2.wiper
  N8: DOIT_ESP32.SCL, photoresistor.P$1, R5.Pin_0
  N9: LED2.cathode, R3.Pin_0

notes:
  [DHT11 GPIO 5
  LED RED GPIO 19
  LED Green GPIO 18
  BUZZ GPIO 21
  光敏電阻 ADC1_CH0 (GPIO36)
  10k可變電阻 ADC1_CH3 (GPIO39)

custom parts:
  DHT11 Humitidy and Temperature Sensor: DHT11 Humidity and Temperature Sensor
